// Logisim project Parity.circ as structural Verilog: 3 circuits, main circuit ParityGenerator
module XOR (
  input  X,
  input  Y,
  input  X_2,
  input  Y_2,
  output out_5,
  output out_6
);

  wire and_1_out, and_3_out, and_4_out, not_1_out, not_2_out, not_3_out, or_1_out;

  not not_1 (not_1_out, X_2);
  not not_2 (not_2_out, and_1_out);
  and and_1 (and_1_out, Y, X);
  or or_1 (or_1_out, Y, X);
  not not_3 (not_3_out, Y_2);
  and and_2 (out_5, not_2_out, or_1_out);
  and and_3 (and_3_out, not_3_out, X_2);
  and and_4 (and_4_out, Y_2, not_1_out);
  or or_2 (out_6, and_3_out, and_4_out);

  // Notes on the sheet:
  //   x XOR y = (x or y) and not (x and y)
  //   Minterm Expansion
  //   Both circuits are equivalent and valid representations of x XOR y
endmodule

module MyXOR (
);


  // Notes on the sheet:
  //   Practice using Logism by recreating one of the implementations from XOR!
endmodule

module ParityGenerator (
  input  X,
  input  Y,
  input  Z,
  output Parity
);

  wire and_1_out, and_2_out, and_3_out, not_1_out, not_2_out, or_1_out, or_2_out;

  and and_1 (and_1_out, X, Y);
  not not_1 (not_1_out, and_1_out);
  or or_1 (or_1_out, Y, X);
  and and_2 (and_2_out, or_1_out, not_1_out);
  and and_3 (and_3_out, Z, and_2_out);
  or or_2 (or_2_out, Z, and_2_out);
  not not_2 (not_2_out, and_3_out);
  and and_4 (Parity, or_2_out, not_2_out);

  // Notes on the sheet:
  //   Input Bits
  //   CINDY ZHANG I PLEDGE MY HONOR THAT I HAVE ABIDED BY THE STEVENS HONOR SYSTEM.
  //   Output Bit
endmodule
